# Fritzing sketch Timing Gate (saved by Fritzing 0.9.3b)

parts:
  R1 = BBC MicroBit
  J1 = Infrared Proximity Sensor
  J2 = Infrared Proximity Sensor
  BATT1 = 4xAA Switchable Battery Pack w/Bare Wire

nets:
  GND: R1.GND, J1.GND, J2.GND, BATT1.NEG
  N1: R1.P1_ANALOG_IN, J2.Vout
  N2: R1.P0_ANALOG_IN, J1.Vout
  VCC: J1.Vcc, J2.Vcc, BATT1.POS

notes:
  I used a micro USB breakout board, which enabled me to use a normal USB lead to provide 5V power from my desk power supply. Power from the power supply goes to each sensor, then the Ground (black wire) for each sensor is connected to the Ground of the micro:bit and this power supply. This creates common ground.
  Start Gate
  End Gate

custom parts:
  BBC MicroBit: The BBC MICRO:BIT
  4xAA Switchable Battery Pack w/Bare Wire: 4xAA Switchable Battery Pack with Bare Wire connection
